// Logisim project 2i.circ as structural Verilog: 1 circuit, main circuit main
module main (
  input  in_1,
  input  in_2,
  output [7:0] out_3
);

  wire clock_1_out;
  wire [0:0] nor_1_out;

  Register register_1 (.D({out_3[6:0], nor_1_out[0]}), .en(in_1), .Q(out_3), .clk(clock_1_out), .clr(in_2));
  Clock clock_1 (.out(clock_1_out));
  nor nor_1 (nor_1_out[0], out_3[0], out_3[1], out_3[2], out_3[3], out_3[4], out_3[5], out_3[6]);
endmodule
