// Logisim project 4BitSort.circ as structural Verilog: 3 circuits, main circuit 4bit_sort
module _4bit_sort (
  input  [3:0] A,
  input  [3:0] B,
  input  [3:0] C,
  input  [3:0] D,
  output [3:0] _1,
  output [3:0] _2,
  output [3:0] _3,
  output [3:0] _4
);

  wire comparator_1_gt, comparator_2_gt, comparator_3_gt, comparator_4_gt, comparator_5_gt, comparator_6_gt;
  wire [3:0] n4bit_swap_1_o1, n4bit_swap_1_o2, n4bit_swap_2_o1, n4bit_swap_2_o2, n4bit_swap_3_o1,
       n4bit_swap_3_o2, n4bit_swap_4_o1, n4bit_swap_5_o1;

  Comparator #(.width(4), .mode("unsigned")) comparator_1 (.a(A), .b(B), .gt(comparator_1_gt));  // open: eq, lt
  _4bit_swap u_4bit_swap_1 (.I1(A), .I2(B), .in_3(comparator_1_gt), .O1(n4bit_swap_1_o1), .O2(n4bit_swap_1_o2));
  Comparator #(.width(4), .mode("unsigned")) comparator_2 (
    .a(n4bit_swap_1_o2), .b(C), .gt(comparator_2_gt));  // open: eq, lt
  _4bit_swap u_4bit_swap_2 (
    .I1(n4bit_swap_1_o2), .I2(C), .in_3(comparator_2_gt), .O1(n4bit_swap_2_o1), .O2(n4bit_swap_2_o2));
  _4bit_swap u_4bit_swap_3 (
    .I1(n4bit_swap_1_o1), .I2(n4bit_swap_2_o1), .in_3(comparator_3_gt), .O1(n4bit_swap_3_o1),
    .O2(n4bit_swap_3_o2));
  Comparator #(.width(4), .mode("unsigned")) comparator_3 (
    .a(n4bit_swap_1_o1), .b(n4bit_swap_2_o1), .gt(comparator_3_gt));  // open: eq, lt
  _4bit_swap u_4bit_swap_4 (.I1(n4bit_swap_2_o2), .I2(D), .in_3(comparator_4_gt), .O1(n4bit_swap_4_o1), .O2(_4));
  Comparator #(.width(4), .mode("unsigned")) comparator_4 (
    .a(n4bit_swap_2_o2), .b(D), .gt(comparator_4_gt));  // open: eq, lt
  Comparator #(.width(4), .mode("unsigned")) comparator_5 (
    .a(n4bit_swap_3_o2), .b(n4bit_swap_4_o1), .gt(comparator_5_gt));  // open: eq, lt
  _4bit_swap u_4bit_swap_5 (
    .I1(n4bit_swap_3_o2), .I2(n4bit_swap_4_o1), .in_3(comparator_5_gt), .O1(n4bit_swap_5_o1), .O2(_3));
  _4bit_swap u_4bit_swap_6 (.I1(n4bit_swap_3_o1), .I2(n4bit_swap_5_o1), .in_3(comparator_6_gt), .O1(_1), .O2(_2));
  Comparator #(.width(4), .mode("unsigned")) comparator_6 (
    .a(n4bit_swap_3_o1), .b(n4bit_swap_5_o1), .gt(comparator_6_gt));  // open: eq, lt
endmodule

// 4
module _4bit_swap (
  input  [3:0] I1,
  input  [3:0] I2,
  input  in_3,
  output [3:0] O1,
  output [3:0] O2
);

  _1bit_swap u_1bit_swap_1 (.I1(I1[0]), .I2(I2[0]), .S(in_3), .O1(O1[0]), ._02(O2[0]));
  _1bit_swap u_1bit_swap_2 (.I1(I1[1]), .I2(I2[1]), .S(in_3), .O1(O1[1]), ._02(O2[1]));
  _1bit_swap u_1bit_swap_3 (.I1(I1[2]), .I2(I2[2]), .S(in_3), .O1(O1[2]), ._02(O2[2]));
  _1bit_swap u_1bit_swap_4 (.I1(I1[3]), .I2(I2[3]), .S(in_3), .O1(O1[3]), ._02(O2[3]));
endmodule

module _1bit_swap (
  input  I1,
  input  I2,
  input  S,
  output O1,
  output _02
);

  wire not_1_out, or_1_out, or_2_out, or_3_out, or_4_out;

  not not_1 (not_1_out, S);
  or or_1 (or_1_out, I1, S);
  or or_2 (or_2_out, I2, not_1_out);
  or or_3 (or_3_out, I2, S);
  or or_4 (or_4_out, I1, not_1_out);
  and and_1 (O1, or_1_out, or_2_out);
  and and_2 (_02, or_3_out, or_4_out);
endmodule
