// Logisim project CPU - ADD j.circ as structural Verilog: 6 circuits, main circuit main
module main (
  input  Reset,
  output [31:0] out_2,
  output out_3,
  output [4:0] out_4,
  output [31:0] out_5,
  output out_6,
  output [4:0] out_7,
  output [31:0] out_8
);

  wire Br, Bsel, clk, EXTOp, j, less, LUIsel, slt, WDsel, WRsel, zero;
  wire [1:0] ALUOp;
  wire [4:0] bit_extender_1_out;
  wire [31:0] ALU_aluresult, bit_extender_2_out, bit_extender_3_out, EXT_extresult, multiplexer_1_out,
       multiplexer_4_out, multiplexer_5_out, NPC_npc, PC_q, ram_1_data, RF_rd1, shifter_1_out, shifter_2_out,
       shifter_3_out;

  Register #(.width(32)) PC (.D(NPC_npc), .Q(PC_q), .clk(clk), .clr(Reset));  // open: en
  NPC NPC (.PC(PC_q), .Imm(out_2[15:0]), .NPC(NPC_npc), .zero(zero), .Br(Br), .Imm26(out_2[25:0]), .j(j));
  Clock clock_1 (.out(clk));
  // Probe on bit_extender_1_out
  Shifter #(.width(32), .shift("lr")) shifter_1 (.in(PC_q), .\dist (5'b00010), .out(shifter_1_out));
  Bit_Extender #(.in_width(32), .out_width(5)) bit_extender_1 (.in(shifter_1_out), .out(bit_extender_1_out));
  Multiplexer #(.width(32)) multiplexer_1 (
    .in0(ALU_aluresult), .in1(ram_1_data), .out(multiplexer_1_out), .sel(WDsel));  // open: en
  ROM #(.addrWidth(5), .dataWidth(32)) rom_1 (.addr(bit_extender_1_out), .data(out_2));  // open: sel
  Multiplexer #(.width(5)) multiplexer_2 (
    .in0(out_2[20:16]), .in1(out_2[15:11]), .out(out_4), .sel(WRsel));  // open: en
  assign bit_extender_2_out = {{31{1'b0}}, less};  // Bit_Extender bit_extender_2
  EXT EXT (.Imm(out_2[15:0]), .EXTresult(EXT_extresult), .EXTOp(EXTOp));
  assign bit_extender_3_out = {{16{1'b0}}, out_2[15:0]};  // Bit_Extender bit_extender_3
  Multiplexer #(.width(32)) multiplexer_3 (
    .in0(multiplexer_1_out), .in1(bit_extender_2_out), .out(out_5), .sel(slt));  // open: en
  Shifter #(.width(32)) shifter_2 (.in(bit_extender_3_out), .\dist (5'b10000), .out(shifter_2_out));
  RF RF (
    .A1(out_2[25:21]), .A2(out_2[20:16]), .A3(out_4), .WD(out_5), .RD1(RF_rd1), .RD2(out_8), .clk(clk),
    .reset(Reset), .WE(out_3));
  Multiplexer #(.width(32)) multiplexer_4 (
    .in0(EXT_extresult), .in1(shifter_2_out), .out(multiplexer_4_out), .sel(LUIsel));  // open: en
  Multiplexer #(.width(32)) multiplexer_5 (
    .in0(out_8), .in1(multiplexer_4_out), .out(multiplexer_5_out), .sel(Bsel));  // open: en
  control Control (
    .op(out_2[31:26]), .func(out_2[5:0]), .WRsel(WRsel), .WDsel(WDsel), .RFWr(out_3), .EXTOp(EXTOp),
    .Bsel(Bsel), .ALUOp(ALUOp), .DMWr(out_6), .Br(Br), .LUIsel(LUIsel), .j(j), .slt(slt));
  ALU ALU (.A(RF_rd1), .B(multiplexer_5_out), .ALUresult(ALU_aluresult), .zero(zero), .ALUop(ALUOp), .less(less));
  Shifter #(.width(32), .shift("lr")) shifter_3 (.in(ALU_aluresult), .\dist (5'b00010), .out(shifter_3_out));
  Bit_Extender #(.in_width(32), .out_width(5)) bit_extender_4 (.in(shifter_3_out), .out(out_7));
  RAM #(.addrWidth(5), .dataWidth(32), .bus("separate")) ram_1 (
    .addr(out_7), .din(out_8), .data(ram_1_data), .str(out_6), .clk(clk), .clr(Reset));  // open: sel, ld

  // Other names for the same wires on the sheet: DMWr = out_6; funct[5:0] = out_2[5:0]; Imm[15:0] = out_2[15:0];
  //   Imm26[25:0] = out_2[25:0]; Instr[31:0] = out_2; shamt[4:0] = out_2[10:6]; rd[4:0] = out_2[15:11];
  //   rt[4:0] = out_2[20:16]; rs[4:0] = out_2[25:21]; op[5:0] = out_2[31:26]; MWA[4:0] = out_7; MWD[31:0] = out_8;
  //   RFWr = out_3; WA[4:0] = out_4; WD[31:0] = out_5

  // Notes on the sheet:
  //   contents of rom_1 (hex, n*v repeats v):
  //   35081234 35292345 109502a
endmodule

module control (
  input  [5:0] op,
  input  [5:0] func,
  output slt,
  output j,
  output WRsel,
  output WDsel,
  output RFWr,
  output EXTOp,
  output Bsel,
  output DMWr,
  output Br,
  output LUIsel,
  output [1:0] ALUOp
);

  wire addu, comparator_2_eq, comparator_8_eq, comparator_9_eq, comparator_10_eq, subu;

  Comparator #(.width(6), .mode("unsigned")) comparator_1 (.a(op), .b(6'b000010), .eq(j));  // open: gt, lt
  Comparator #(.width(6), .mode("unsigned")) comparator_2 (
    .a(op), .b({6{1'b0}}), .eq(comparator_2_eq));  // open: gt, lt
  Comparator #(.width(6), .mode("unsigned")) comparator_3 (.a(op), .b(6'b001101), .eq(ALUOp[1]));  // open: gt, lt
  Comparator #(.width(6), .mode("unsigned")) comparator_4 (.a(op), .b(6'b100011), .eq(WDsel));  // open: gt, lt
  Comparator #(.width(6), .mode("unsigned")) comparator_5 (.a(op), .b(6'b101011), .eq(DMWr));  // open: gt, lt
  Comparator #(.width(6), .mode("unsigned")) comparator_6 (.a(op), .b(6'b000100), .eq(Br));  // open: gt, lt
  Comparator #(.width(6), .mode("unsigned")) comparator_7 (.a(op), .b(6'b001111), .eq(LUIsel));  // open: gt, lt
  Comparator #(.width(6), .mode("unsigned")) comparator_8 (
    .a(func), .b(6'b100001), .eq(comparator_8_eq));  // open: gt, lt
  Comparator #(.width(6), .mode("unsigned")) comparator_9 (
    .a(func), .b(6'b100011), .eq(comparator_9_eq));  // open: gt, lt
  Comparator #(.width(6), .mode("unsigned")) comparator_10 (
    .a(func), .b(6'b101010), .eq(comparator_10_eq));  // open: gt, lt
  and and_1 (slt, comparator_10_eq, comparator_2_eq);
  and and_2 (addu, comparator_2_eq, comparator_8_eq);
  and and_3 (subu, comparator_2_eq, comparator_9_eq);
  or or_1 (WRsel, addu, slt, subu);
  or or_2 (RFWr, slt, addu, subu, ALUOp[1], WDsel, LUIsel);
  or or_3 (EXTOp, WDsel, DMWr);
  or or_4 (Bsel, ALUOp[1], LUIsel, WDsel, DMWr);
  or or_5 (ALUOp[0], subu, Br, slt);

  // Other names for the same wires on the sheet: ori = ALUOp[1]; beq = Br; lui = LUIsel; lw = WDsel; sw = DMWr
endmodule

module NPC (
  input  [31:0] PC,
  input  [15:0] Imm,
  input  j,
  input  Br,
  input  zero,
  input  [25:0] Imm26,
  output [31:0] NPC
);

  wire and_1_out;
  wire [31:0] adder_1_out, adder_2_out, bit_extender_1_out, bit_extender_2_out, multiplexer_1_out,
       shifter_1_out, shifter_2_out, subtractor_1_out;

  Adder #(.width(32)) adder_1 (.a(32'h4), .b(PC), .out(adder_1_out));  // open: cin, cout
  assign bit_extender_1_out = {{16{Imm[15]}}, Imm};  // Bit_Extender bit_extender_1
  assign bit_extender_2_out = {{6{1'b0}}, Imm26};  // Bit_Extender bit_extender_2
  Shifter #(.width(32)) shifter_1 (.in(bit_extender_1_out), .\dist (5'b00010), .out(shifter_1_out));
  Shifter #(.width(32)) shifter_2 (.in(bit_extender_2_out), .\dist (5'b00010), .out(shifter_2_out));
  Adder #(.width(32)) adder_2 (.a(adder_1_out), .b(shifter_1_out), .out(adder_2_out));  // open: cin, cout
  and and_1 (and_1_out, zero, Br);
  Multiplexer #(.width(32)) multiplexer_1 (
    .in0(adder_1_out), .in1(adder_2_out), .out(multiplexer_1_out), .sel(and_1_out));  // open: en
  Subtractor #(.width(32)) subtractor_1 (.a(shifter_2_out), .b(32'h3000), .out(subtractor_1_out));  // open: bin, bout
  Multiplexer #(.width(32)) multiplexer_2 (
    .in0(multiplexer_1_out), .in1(subtractor_1_out), .out(NPC), .sel(j));  // open: en
endmodule

module RF (
  input  WE,
  input  clk,
  input  reset,
  input  [4:0] A1,
  input  [4:0] A2,
  input  [4:0] A3,
  input  [31:0] WD,
  output [31:0] RD1,
  output [31:0] RD2
);

  wire e0, e1, e2, e3, e4, e5, e6, e7, e8, e9, e10, e11, e12, e13, e14, e15, e16, e17, e18, e19, e20, e21,
       e22, e23, e24, e25, e26, e27, e28, e29, e30, e31;
  wire [31:0] i0, i1, i2, i3, i4, i5, i6, i7, i8, i9, i10, i11, i12, i13, i14, i15, i16, i17, i18, i19, i20,
       i21, i22, i23, i24, i25, i26, i27, i28, i29, i30, i31, o0, o1, o2, o3, o4, o5, o6, o7, o8, o9, o10,
       o11, o12, o13, o14, o15, o16, o17, o18, o19, o20, o21, o22, o23, o24, o25, o26, o27, o28, o29, o30,
       o31;

  // Probe on i0
  Demultiplexer #(.select(5), .width(32), .disabled(0)) demultiplexer_1 (
    .out0(i0), .out1(i1), .out2(i2), .out3(i3), .out4(i4), .out5(i5), .out6(i6), .out7(i7), .out8(i8),
    .out9(i9), .out10(i10), .out11(i11), .out12(i12), .out13(i13), .out14(i14), .out15(i15), .out16(i16),
    .out17(i17), .out18(i18), .out19(i19), .out20(i20), .out21(i21), .out22(i22), .out23(i23), .out24(i24),
    .out25(i25), .out26(i26), .out27(i27), .out28(i28), .out29(i29), .out30(i30), .out31(i31), .in(WD),
    .sel(A3));  // open: en
  Register #(.width(32)) register_1 (.D(i0), .en(e0), .Q(o0), .clk(clk), .clr(1'b1));
  Register #(.width(32)) register_2 (.D(i4), .en(e4), .Q(o4), .clk(clk), .clr(reset));
  Register #(.width(32)) register_3 (.D(i8), .en(e8), .Q(o8), .clk(clk), .clr(reset));
  Register #(.width(32)) register_4 (.D(i12), .en(e12), .Q(o12), .clk(clk), .clr(reset));
  Register #(.width(32)) register_5 (.D(i16), .en(e16), .Q(o16), .clk(clk), .clr(reset));
  Register #(.width(32)) register_6 (.D(i20), .en(e20), .Q(o20), .clk(clk), .clr(reset));
  Register #(.width(32)) register_7 (.D(i24), .en(e24), .Q(o24), .clk(clk), .clr(reset));
  Register #(.width(32)) register_8 (.D(i28), .en(e28), .Q(o28), .clk(clk), .clr(reset));
  Register #(.width(32)) register_9 (.D(i1), .en(e1), .Q(o1), .clk(clk), .clr(reset));
  Register #(.width(32)) register_10 (.D(i5), .en(e5), .Q(o5), .clk(clk), .clr(reset));
  Register #(.width(32)) register_11 (.D(i9), .en(e9), .Q(o9), .clk(clk), .clr(reset));
  Register #(.width(32)) register_12 (.D(i13), .en(e13), .Q(o13), .clk(clk), .clr(reset));
  Register #(.width(32)) register_13 (.D(i17), .en(e17), .Q(o17), .clk(clk), .clr(reset));
  Register #(.width(32)) register_14 (.D(i21), .en(e21), .Q(o21), .clk(clk), .clr(reset));
  Register #(.width(32)) register_15 (.D(i25), .en(e25), .Q(o25), .clk(clk), .clr(reset));
  Register #(.width(32)) register_16 (.D(i29), .en(e29), .Q(o29), .clk(clk), .clr(reset));
  Register #(.width(32)) register_17 (.D(i2), .en(e2), .Q(o2), .clk(clk), .clr(reset));
  Register #(.width(32)) register_18 (.D(i6), .en(e6), .Q(o6), .clk(clk), .clr(reset));
  Register #(.width(32)) register_19 (.D(i10), .en(e10), .Q(o10), .clk(clk), .clr(reset));
  Register #(.width(32)) register_20 (.D(i14), .en(e14), .Q(o14), .clk(clk), .clr(reset));
  Register #(.width(32)) register_21 (.D(i18), .en(e18), .Q(o18), .clk(clk), .clr(reset));
  Register #(.width(32)) register_22 (.D(i22), .en(e22), .Q(o22), .clk(clk), .clr(reset));
  Register #(.width(32)) register_23 (.D(i26), .en(e26), .Q(o26), .clk(clk), .clr(reset));
  Register #(.width(32)) register_24 (.D(i30), .en(e30), .Q(o30), .clk(clk), .clr(reset));
  Demultiplexer #(.select(5), .disabled(0)) demultiplexer_2 (
    .out0(e0), .out1(e1), .out2(e2), .out3(e3), .out4(e4), .out5(e5), .out6(e6), .out7(e7), .out8(e8),
    .out9(e9), .out10(e10), .out11(e11), .out12(e12), .out13(e13), .out14(e14), .out15(e15), .out16(e16),
    .out17(e17), .out18(e18), .out19(e19), .out20(e20), .out21(e21), .out22(e22), .out23(e23), .out24(e24),
    .out25(e25), .out26(e26), .out27(e27), .out28(e28), .out29(e29), .out30(e30), .out31(e31), .in(WE),
    .sel(A3));  // open: en
  Register #(.width(32)) register_25 (.D(i3), .en(e3), .Q(o3), .clk(clk), .clr(reset));
  Register #(.width(32)) register_26 (.D(i7), .en(e7), .Q(o7), .clk(clk), .clr(reset));
  Register #(.width(32)) register_27 (.D(i11), .en(e11), .Q(o11), .clk(clk), .clr(reset));
  Register #(.width(32)) register_28 (.D(i15), .en(e15), .Q(o15), .clk(clk), .clr(reset));
  Register #(.width(32)) register_29 (.D(i19), .en(e19), .Q(o19), .clk(clk), .clr(reset));
  Register #(.width(32)) register_30 (.D(i23), .en(e23), .Q(o23), .clk(clk), .clr(reset));
  Register #(.width(32)) register_31 (.D(i27), .en(e27), .Q(o27), .clk(clk), .clr(reset));
  Register #(.width(32)) register_32 (.D(i31), .en(e31), .Q(o31), .clk(clk), .clr(reset));
  Multiplexer #(.select(5), .width(32)) multiplexer_1 (
    .in0(o0), .in1(o1), .in2(o2), .in3(o3), .in4(o4), .in5(o5), .in6(o6), .in7(o7), .in8(o8), .in9(o9),
    .in10(o10), .in11(o11), .in12(o12), .in13(o13), .in14(o14), .in15(o15), .in16(o16), .in17(o17),
    .in18(o18), .in19(o19), .in20(o20), .in21(o21), .in22(o22), .in23(o23), .in24(o24), .in25(o25),
    .in26(o26), .in27(o27), .in28(o28), .in29(o29), .in30(o30), .in31(o31), .out(RD1), .sel(A1));  // open: en
  Multiplexer #(.select(5), .width(32)) multiplexer_2 (
    .in0(o0), .in1(o1), .in2(o2), .in3(o3), .in4(o4), .in5(o5), .in6(o6), .in7(o7), .in8(o8), .in9(o9),
    .in10(o10), .in11(o11), .in12(o12), .in13(o13), .in14(o14), .in15(o15), .in16(o16), .in17(o17),
    .in18(o18), .in19(o19), .in20(o20), .in21(o21), .in22(o22), .in23(o23), .in24(o24), .in25(o25),
    .in26(o26), .in27(o27), .in28(o28), .in29(o29), .in30(o30), .in31(o31), .out(RD2), .sel(A2));  // open: en

  // Other names for the same wires on the sheet: clean = reset
endmodule

module ALU (
  input  [31:0] A,
  input  [31:0] B,
  input  [1:0] ALUop,
  output zero,
  output less,
  output [31:0] ALUresult
);

  wire [31:0] adder_1_out, or_1_out, subtractor_1_out;

  Adder #(.width(32)) adder_1 (.a(A), .b(B), .out(adder_1_out));  // open: cin, cout
  Subtractor #(.width(32)) subtractor_1 (.a(A), .b(B), .out(subtractor_1_out));  // open: bin, bout
  assign or_1_out = A | B;  // OR_Gate or_1, 32 bits wide
  Multiplexer #(.select(2), .width(32)) multiplexer_1 (
    .in0(adder_1_out), .in1(subtractor_1_out), .in2(or_1_out), .out(ALUresult), .sel(ALUop));  // open: in3, en
  Comparator #(.width(32)) comparator_1 (.a({32{1'b0}}), .b(ALUresult), .gt(less), .eq(zero));  // open: lt
endmodule

module EXT (
  input  [15:0] Imm,
  input  EXTOp,
  output [31:0] EXTresult
);

  wire [31:0] bit_extender_1_out, bit_extender_2_out;

  assign bit_extender_1_out = {{16{1'b0}}, Imm};  // Bit_Extender bit_extender_1
  assign bit_extender_2_out = {{16{Imm[15]}}, Imm};  // Bit_Extender bit_extender_2
  Multiplexer #(.width(32)) multiplexer_1 (
    .in0(bit_extender_1_out), .in1(bit_extender_2_out), .out(EXTresult), .sel(EXTOp));  // open: en
endmodule
