// Logisim project CRC.circ as structural Verilog: 2 circuits, main circuit CRC
module CRC (
  input  [7:0] in_1,
  input  [3:0] in_2,
  output [10:0] out_3
);

  wire [10:0] step_1_out_4, step_2_out_4, step_3_out_4, step_4_out_4, step_5_out_4, step_6_out_4,
       step_7_out_4;
  wire [10:3] step_8_out_4;

  step step_1 (.data({in_1, 3'b000}), .chushu(in_2), .sel_which(4'b1010), .out_4(step_1_out_4));
  step step_2 (.data(step_1_out_4), .chushu(in_2), .sel_which(4'b1001), .out_4(step_2_out_4));
  step step_3 (.data(step_2_out_4), .chushu(in_2), .sel_which(4'b1000), .out_4(step_3_out_4));
  step step_4 (.data(step_3_out_4), .chushu(in_2), .sel_which(4'b0111), .out_4(step_4_out_4));
  step step_5 (.data(step_4_out_4), .chushu(in_2), .sel_which(4'b0110), .out_4(step_5_out_4));
  step step_6 (.data(step_5_out_4), .chushu(in_2), .sel_which(4'b0101), .out_4(step_6_out_4));
  step step_7 (.data(step_6_out_4), .chushu(in_2), .sel_which(4'b0100), .out_4(step_7_out_4));
  step step_8 (.data(step_7_out_4), .chushu(in_2), .sel_which(4'b0011), .out_4({step_8_out_4, out_3[2:0]}));

  assign out_3[10:3] = in_1;
endmodule

module step (
  input  [10:0] data,
  input  [3:0] chushu,
  input  [3:0] sel_which,
  output [10:0] out_4
);

  wire bitselector_1_out;
  wire [3:0] multiplexer_1_out, subtractor_1_out;
  wire [10:0] bit_extender_1_out, shifter_1_out;

  BitSelector #(.width(11)) bitselector_1 (.in(data), .out(bitselector_1_out), .sel(sel_which));
  Multiplexer #(.width(4)) multiplexer_1 (
    .in0(4'b0000), .in1(chushu), .out(multiplexer_1_out), .sel(bitselector_1_out));  // open: en
  Subtractor #(.width(4)) subtractor_1 (.a(sel_which), .b(4'b0011), .out(subtractor_1_out));  // open: bin, bout
  assign bit_extender_1_out = {{7{1'b0}}, multiplexer_1_out};  // Bit_Extender bit_extender_1
  Shifter #(.width(11)) shifter_1 (.in(bit_extender_1_out), .\dist (subtractor_1_out), .out(shifter_1_out));
  assign out_4 = shifter_1_out ^ data;  // XOR_Gate xor_1, 11 bits wide
endmodule
