// Logisim project add.circ as structural Verilog: 2 circuits, main circuit main
module main (
  input  [7:0] in_1,
  input  [7:0] in_2,
  output [7:0] out_3
);

  wire add_1_1_cout, add_1_1_sum, bitselector_1_out, bitselector_2_out, clock_1_out, comparator_1_eq,
       not_1_out, register_1_q;
  wire [2:0] counter_1_q;

  Clock clock_1 (.out(clock_1_out));
  BitSelector bitselector_1 (.in(in_1), .out(bitselector_1_out), .sel(counter_1_q));
  BitSelector bitselector_2 (.in(in_2), .out(bitselector_2_out), .sel(counter_1_q));
  Counter #(.width(3), .max('h7), .ongoal("stay")) counter_1 (
    .Q(counter_1_q), .clk(clock_1_out));  // open: load, D, count, carry, clr
  add_1 add_1_1 (
    .a(bitselector_1_out), .b(bitselector_2_out), .cin(register_1_q), .sum(add_1_1_sum), .cout(add_1_1_cout));
  Register #(.width(1)) register_1 (
    .D(add_1_1_cout), .Q(register_1_q), .clk(clock_1_out), .clr(not_1_out));  // open: en
  Demultiplexer #(.select(3)) demultiplexer_1 (
    .out0(out_3[0]), .out1(out_3[1]), .out2(out_3[2]), .out3(out_3[3]), .out4(out_3[4]), .out5(out_3[5]),
    .out6(out_3[6]), .out7(out_3[7]), .in(add_1_1_sum), .sel(counter_1_q));  // open: en
  Comparator #(.width(3)) comparator_1 (.a(counter_1_q), .b(3'b111), .eq(comparator_1_eq));  // open: gt, lt
  not not_1 (not_1_out, comparator_1_eq);
endmodule

module add_1 (
  input  a,
  input  b,
  input  cin,
  output sum,
  output cout
);

  wire and_1_out, and_2_out, and_3_out, and_4_out, and_5_out, and_6_out, and_7_out, not_1_out, not_2_out,
       not_3_out, not_4_out, not_5_out, not_6_out;

  not not_1 (not_1_out, a);
  not not_2 (not_2_out, b);
  not not_3 (not_3_out, a);
  not not_4 (not_4_out, cin);
  not not_5 (not_5_out, b);
  not not_6 (not_6_out, cin);
  and and_1 (and_1_out, b, cin);
  and and_2 (and_2_out, a, cin);
  and and_3 (and_3_out, a, b);
  and and_4 (and_4_out, not_1_out, not_2_out, cin);
  and and_5 (and_5_out, not_3_out, b, not_4_out);
  and and_6 (and_6_out, a, not_5_out, not_6_out);
  and and_7 (and_7_out, a, b, cin);
  or or_1 (cout, and_1_out, and_2_out, and_3_out);
  or or_2 (sum, and_4_out, and_5_out, and_6_out, and_7_out);
endmodule
