// Logisim project fsm.circ as structural Verilog: 2 circuits, main circuit fsm
module fsm (
  input  in_1,
  input  [1:0] in_2,
  output out_3
);

  wire clock_1_out, not_1_out, register_2_q, s_move_1_find;
  wire [1:0] register_1_q, s_move_1_sout;

  Clock clock_1 (.out(clock_1_out));
  s_move s_move_1 (.in(in_2), .sin(register_1_q), .sout(s_move_1_sout), .find(s_move_1_find));
  Register #(.width(2)) register_1 (
    .D(s_move_1_sout), .Q(register_1_q), .clk(clock_1_out), .clr(register_2_q));  // open: en
  buf buffer_1 (out_3, s_move_1_find);
  Register #(.width(1)) register_2 (.D(in_1), .Q(register_2_q), .clk(clock_1_out), .clr(not_1_out));  // open: en
  not not_1 (not_1_out, in_1);
endmodule

module s_move (
  input  [1:0] in,
  input  [1:0] sin,
  output [1:0] sout,
  output find
);

  wire and_1_out, and_2_out, and_3_out, and_4_out, not_1_out, not_2_out, not_3_out, not_4_out, not_5_out,
       not_6_out, not_7_out, not_8_out, not_9_out;

  not not_1 (not_1_out, in[0]);
  not not_2 (not_2_out, sin[1]);
  not not_3 (not_3_out, in[0]);
  not not_4 (not_4_out, sin[0]);
  not not_5 (not_5_out, in[0]);
  not not_6 (not_6_out, sin[0]);
  not not_7 (not_7_out, in[1]);
  not not_8 (not_8_out, in[0]);
  not not_9 (not_9_out, sin[0]);
  and and_1 (and_1_out, not_1_out, not_2_out, sin[0]);
  and and_2 (and_2_out, not_3_out, sin[1], not_4_out);
  and and_3 (and_3_out, not_5_out, sin[1], not_6_out);
  and and_4 (and_4_out, not_7_out, in[0]);
  and and_5 (find, not_8_out, sin[1], not_9_out);
  or or_1 (sout[1], and_1_out, and_2_out);
  or or_2 (sout[0], and_3_out, and_4_out);
endmodule
