// Logisim project ftoi.circ as structural Verilog: 1 circuit, main circuit ftoi
module ftoi (
  input  [15:0] in_1,
  output [31:0] out_2
);

  wire comparator_1_eq, comparator_2_eq, comparator_3_lt, comparator_4_lt;
  wire [3:0] bit_extender_2_out, bit_extender_3_out;
  wire [4:0] subtractor_1_out, subtractor_2_out, subtractor_3_out;
  wire [10:10] nor_1_out;
  wire [15:0] bit_extender_1_out, multiplexer_1_out, multiplexer_2_out, multiplexer_3_out, shifter_1_out,
       shifter_2_out;
  wire [31:0] bit_extender_4_out, subtractor_4_out;

  Comparator #(.width(5), .mode("unsigned")) comparator_1 (
    .a({5{1'b1}}), .b(in_1[14:10]), .eq(comparator_1_eq));  // open: gt, lt
  Subtractor #(.width(5)) subtractor_1 (.a(in_1[14:10]), .b(5'b01111), .out(subtractor_1_out));  // open: bin, bout
  assign bit_extender_1_out = {{5{1'b0}}, {nor_1_out[10], in_1[9:0]}};  // Bit_Extender bit_extender_1
  nor nor_1 (nor_1_out[10], comparator_1_eq, comparator_2_eq);
  Comparator #(.width(5), .mode("unsigned")) comparator_2 (
    .a({5{1'b0}}), .b(in_1[14:10]), .eq(comparator_2_eq));  // open: gt, lt
  Comparator #(.width(5)) comparator_3 (.a(subtractor_1_out), .b({5{1'b0}}), .lt(comparator_3_lt));  // open: gt, eq
  Shifter #(.width(16)) shifter_1 (.in(bit_extender_1_out), .\dist (bit_extender_2_out), .out(shifter_1_out));
  Shifter #(.width(16), .shift("lr")) shifter_2 (
    .in(bit_extender_1_out), .\dist (bit_extender_3_out), .out(shifter_2_out));
  Subtractor #(.width(5)) subtractor_2 (.a(subtractor_1_out), .b(5'b01010), .out(subtractor_2_out));  // open: bin, bout
  Bit_Extender #(.in_width(5), .out_width(4)) bit_extender_2 (.in(subtractor_2_out), .out(bit_extender_2_out));
  Multiplexer #(.width(16)) multiplexer_1 (
    .in0(shifter_1_out), .in1(shifter_2_out), .out(multiplexer_1_out), .sel(comparator_4_lt));  // open: en
  Comparator #(.width(5)) comparator_4 (.a(subtractor_2_out), .b({5{1'b0}}), .lt(comparator_4_lt));  // open: gt, eq
  Subtractor #(.width(5)) subtractor_3 (
    .a({5{1'b0}}), .b(subtractor_2_out), .out(subtractor_3_out));  // open: bin, bout
  Bit_Extender #(.in_width(5), .out_width(4)) bit_extender_3 (.in(subtractor_3_out), .out(bit_extender_3_out));
  Multiplexer #(.width(16)) multiplexer_2 (
    .in0(multiplexer_1_out), .in1({16{1'b0}}), .out(multiplexer_2_out), .sel(comparator_3_lt));  // open: en
  Multiplexer #(.width(16)) multiplexer_3 (
    .in0(multiplexer_2_out), .in1({16{1'b0}}), .out(multiplexer_3_out), .sel(comparator_1_eq));  // open: en
  assign bit_extender_4_out = {{16{1'b0}}, multiplexer_3_out};  // Bit_Extender bit_extender_4
  Subtractor #(.width(32)) subtractor_4 (
    .a({32{1'b0}}), .b(bit_extender_4_out), .out(subtractor_4_out));  // open: bin, bout
  Multiplexer #(.width(32)) multiplexer_4 (
    .in0(bit_extender_4_out), .in1(subtractor_4_out), .out(out_2), .sel(in_1[15]));  // open: en
endmodule
