// Logisim project mod5.circ as structural Verilog: 2 circuits, main circuit mod5
module mod5 (
  input  in_1,
  output out_2,
  output out_3,
  output out_4,
  output out_5,
  output out_6
);

  wire clock_1_out;
  wire [1:0] cul_1_m0, register_1_q;

  cul cul_1 (
    .In(in_1), .S1(register_1_q[1]), .S0(register_1_q[0]), .s4(out_6), .s3(out_5), .s2(out_4), .s1_2(out_3),
    .s0_2(out_2), .m1(cul_1_m0[1]), .m0(cul_1_m0[0]));
  Register #(.width(2)) register_1 (.D(cul_1_m0), .Q(register_1_q), .clk(clock_1_out));  // open: en, clr
  Clock clock_1 (.out(clock_1_out));
endmodule

module cul (
  input  In,
  input  S1,
  input  S0,
  output s4,
  output s3,
  output s2,
  output s1_2,
  output s0_2,
  output m1,
  output m0
);

  wire and_1_out, and_2_out, and_3_out, and_4_out, and_5_out, and_6_out, and_7_out, and_8_out, and_9_out,
       and_10_out, and_11_out, and_12_out, and_13_out, and_14_out, not_1_out, not_2_out, not_3_out,
       not_4_out, not_5_out, not_6_out, not_7_out, not_8_out, not_9_out, not_10_out, not_11_out, not_12_out,
       not_13_out, not_14_out, not_15_out, not_16_out, not_17_out, not_18_out, not_19_out, not_20_out;

  not not_1 (not_1_out, In);
  not not_2 (not_2_out, S1);
  not not_3 (not_3_out, In);
  not not_4 (not_4_out, S0);
  not not_5 (not_5_out, S1);
  not not_6 (not_6_out, S0);
  not not_7 (not_7_out, S1);
  not not_8 (not_8_out, S0);
  not not_9 (not_9_out, In);
  not not_10 (not_10_out, S1);
  not not_11 (not_11_out, S0);
  not not_12 (not_12_out, In);
  not not_13 (not_13_out, S1);
  not not_14 (not_14_out, S0);
  not not_15 (not_15_out, In);
  not not_16 (not_16_out, S1);
  not not_17 (not_17_out, In);
  not not_18 (not_18_out, S0);
  not not_19 (not_19_out, S1);
  not not_20 (not_20_out, S0);
  and and_1 (and_1_out, not_1_out, not_2_out, S0);
  and and_2 (and_2_out, not_3_out, S1, not_4_out);
  and and_3 (and_3_out, In, not_5_out, S0);
  and and_4 (and_4_out, In, S1, not_6_out);
  and and_5 (and_5_out, In, not_7_out, not_8_out);
  and and_6 (and_6_out, In, S1, S0);
  and and_7 (and_7_out, not_9_out, not_10_out, not_11_out);
  and and_8 (and_8_out, not_12_out, S1, S0);
  and and_9 (and_9_out, not_13_out, S0);
  and and_10 (and_10_out, S1, not_14_out);
  and and_11 (and_11_out, not_15_out, not_16_out, S0);
  and and_12 (and_12_out, not_17_out, S1, not_18_out);
  and and_13 (and_13_out, In, not_19_out, not_20_out);
  and and_14 (and_14_out, In, S1, S0);
  or or_1 (s4, and_1_out, and_2_out);
  or or_2 (s3, and_3_out, and_4_out);
  or or_3 (s2, and_5_out, and_6_out);
  or or_4 (s1_2, and_7_out, and_8_out);
  or or_5 (m1, and_9_out, and_10_out);
  or or_6 (m0, and_11_out, and_12_out, and_13_out, and_14_out);

  assign s0_2 = 1'b0;
endmodule
