// Logisim project swap.circ as structural Verilog: 1 circuit, main circuit swap
module swap (
  input  I1,
  input  I2,
  input  S,
  output O1,
  output _02
);

  wire not_1_out, or_1_out, or_2_out, or_3_out, or_4_out;

  not not_1 (not_1_out, S);
  or or_1 (or_1_out, I1, S);
  or or_2 (or_2_out, I2, not_1_out);
  or or_3 (or_3_out, I2, S);
  or or_4 (or_4_out, I1, not_1_out);
  and and_1 (O1, or_1_out, or_2_out);
  and and_2 (_02, or_3_out, or_4_out);
endmodule
