// Logisim project mod.circ as structural Verilog
module \转移  (
  input  c1,
  input  c0,
  input  b,
  output a1,
  output a0
);

  wire and_1_out, and_2_out, and_3_out, and_4_out, and_5_out, and_6_out, not_1_out, not_2_out, not_3_out,
       not_4_out, not_5_out, not_6_out, not_7_out, not_8_out;

  not not_1 (not_1_out, c1);
  not not_2 (not_2_out, c0);
  not not_3 (not_3_out, c1);
  not not_4 (not_4_out, c0);
  not not_5 (not_5_out, c1);
  not not_6 (not_6_out, b);
  not not_7 (not_7_out, c0);
  not not_8 (not_8_out, b);
  and and_1 (and_1_out, not_1_out, c0);
  and and_2 (and_2_out, c1, not_2_out);
  and and_3 (and_3_out, not_3_out, not_4_out, b);
  and and_4 (and_4_out, not_5_out, c0, not_6_out);
  and and_5 (and_5_out, c1, not_7_out, not_8_out);
  and and_6 (and_6_out, c1, c0, b);
  or or_1 (a1, and_1_out, and_2_out);
  or or_2 (a0, and_3_out, and_4_out, and_5_out, and_6_out);
endmodule

module \输出  (
  input  in_1,
  input  a2,
  output s0,
  output s1,
  output s2,
  output s3,
  output s4
);

  wire not_1_out, not_2_out, not_3_out, not_4_out;

  not not_1 (not_1_out, in_1);
  not not_2 (not_2_out, a2);
  not not_3 (not_3_out, in_1);
  not not_4 (not_4_out, a2);
  and and_1 (s4, in_1, a2);
  and and_2 (s1, not_1_out, not_2_out);
  and and_3 (s2, not_3_out, a2);
  and and_4 (s3, in_1, not_4_out);

  assign s0 = 1'b0;
endmodule
