// Logisim project 啊啊啊.circ as structural Verilog: 8 circuits, main circuit main
module main (
  input  [31:0] in_1,
  output [31:0] out_2
);

  wire \计数逻辑_1_out_2 , \计数逻辑_1_out_3 ;

  \计数逻辑  \u_计数逻辑_1  (.in_1(in_1), .out_2(\计数逻辑_1_out_2 ), .out_3(\计数逻辑_1_out_3 ));
  \计算  \u_计算_1  (.in_1(\计数逻辑_1_out_2 ), .in_2(\计数逻辑_1_out_3 ), .out_3(out_2));
endmodule

module \矩阵乘法  (
  input  [31:0] in_1,
  input  [31:0] in_2,
  input  [31:0] in_3,
  input  [31:0] in_4,
  input  [31:0] in_5,
  input  [31:0] in_6,
  input  [31:0] in_7,
  input  [31:0] in_8,
  output [31:0] out_9,
  output [31:0] out_10,
  output [31:0] out_11,
  output [31:0] out_12
);

  wire [31:0] multiplier_1_cout, multiplier_1_out, multiplier_2_out, multiplier_3_cout, multiplier_3_out,
       multiplier_4_out, multiplier_5_cout, multiplier_5_out, multiplier_6_out, multiplier_7_cout,
       multiplier_7_out, multiplier_8_out;

  Multiplier #(.width(32)) multiplier_1 (
    .a(in_1), .b(in_5), .out(multiplier_1_out), .cout(multiplier_1_cout));  // open: cin
  Multiplier #(.width(32)) multiplier_2 (
    .a(in_2), .b(in_7), .out(multiplier_2_out), .cin(multiplier_1_cout));  // open: cout
  Multiplier #(.width(32)) multiplier_3 (
    .a(in_1), .b(in_6), .out(multiplier_3_out), .cout(multiplier_3_cout));  // open: cin
  Multiplier #(.width(32)) multiplier_4 (
    .a(in_2), .b(in_8), .out(multiplier_4_out), .cin(multiplier_3_cout));  // open: cout
  Multiplier #(.width(32)) multiplier_5 (
    .a(in_3), .b(in_5), .out(multiplier_5_out), .cout(multiplier_5_cout));  // open: cin
  Multiplier #(.width(32)) multiplier_6 (
    .a(in_4), .b(in_7), .out(multiplier_6_out), .cin(multiplier_5_cout));  // open: cout
  Multiplier #(.width(32)) multiplier_7 (
    .a(in_3), .b(in_6), .out(multiplier_7_out), .cout(multiplier_7_cout));  // open: cin
  Multiplier #(.width(32)) multiplier_8 (
    .a(in_4), .b(in_8), .out(multiplier_8_out), .cin(multiplier_7_cout));  // open: cout
  Adder #(.width(32)) adder_1 (.a(multiplier_1_out), .b(multiplier_2_out), .out(out_9));  // open: cin, cout
  Adder #(.width(32)) adder_2 (.a(multiplier_3_out), .b(multiplier_4_out), .out(out_10));  // open: cin, cout
  Adder #(.width(32)) adder_3 (.a(multiplier_5_out), .b(multiplier_6_out), .out(out_11));  // open: cin, cout
  Adder #(.width(32)) adder_4 (.a(multiplier_7_out), .b(multiplier_8_out), .out(out_12));  // open: cin, cout

  // Other names for the same wires on the sheet: a11[31:0] = in_1; a12[31:0] = in_2; a21[31:0] = in_3;
  //   a22[31:0] = in_4; b11[31:0] = in_5; b12[31:0] = in_6; b21[31:0] = in_7; b22[31:0] = in_8
endmodule

module \矩阵mux  (
  input  [31:0] in_1,
  input  [31:0] in_2,
  input  [31:0] in_3,
  input  [31:0] in_4,
  input  [31:0] in_5,
  input  [31:0] in_6,
  input  [31:0] in_7,
  input  [31:0] in_8,
  input  in_9,
  output [31:0] out_10,
  output [31:0] out_11,
  output [31:0] out_12,
  output [31:0] out_13
);

  Multiplexer #(.width(32)) multiplexer_1 (.in0(in_1), .in1(in_5), .out(out_10), .sel(in_9));  // open: en
  Multiplexer #(.width(32)) multiplexer_2 (.in0(in_2), .in1(in_6), .out(out_11), .sel(in_9));  // open: en
  Multiplexer #(.width(32)) multiplexer_3 (.in0(in_3), .in1(in_7), .out(out_12), .sel(in_9));  // open: en
  Multiplexer #(.width(32)) multiplexer_4 (.in0(in_4), .in1(in_8), .out(out_13), .sel(in_9));  // open: en

  // Other names for the same wires on the sheet: a11[31:0] = in_1; a12[31:0] = in_2; a21[31:0] = in_3;
  //   a22[31:0] = in_4; b11[31:0] = in_5; b12[31:0] = in_6; b21[31:0] = in_7; b22[31:0] = in_8
endmodule

module \矩阵初始值  (
  output [31:0] out_1,
  output [31:0] out_2,
  output [31:0] out_3,
  output [31:0] out_4
);


  assign out_1 = 32'h1;
  assign out_2 = 32'h1;
  assign out_3 = 32'h1;
  assign out_4 = {32{1'b0}};
endmodule

module \计算  (
  input  in_1,
  input  in_2,
  output [31:0] out_3
);

  wire clock_1_out, clock_2_out, counter_1_q, counter_2_q, not_1_out;
  wire [31:0] a11, a12, a21, a22, s11, s12, s21, s22, \单位阵_1_out_1 , \单位阵_1_out_2 , \单位阵_1_out_3 ,
       \单位阵_1_out_4 , \单位阵_2_out_1 , \单位阵_2_out_2 , \单位阵_2_out_3 , \单位阵_2_out_4 , \矩阵mux_1_out_10 ,
       \矩阵mux_1_out_11 , \矩阵mux_1_out_12 , \矩阵mux_1_out_13 , \矩阵mux_2_out_10 , \矩阵mux_2_out_11 ,
       \矩阵mux_2_out_12 , \矩阵mux_2_out_13 , \矩阵mux_3_out_10 , \矩阵mux_3_out_11 , \矩阵mux_3_out_12 ,
       \矩阵mux_3_out_13 , \矩阵乘法_1_out_9 , \矩阵乘法_1_out_10 , \矩阵乘法_1_out_11 , \矩阵乘法_1_out_12 , \矩阵乘法_2_out_9 ,
       \矩阵乘法_2_out_10 , \矩阵乘法_2_out_11 , \矩阵乘法_2_out_12 , \矩阵初始值_1_out_1 , \矩阵初始值_1_out_2 , \矩阵初始值_1_out_3 ,
       \矩阵初始值_1_out_4 ;

  \矩阵初始值  \u_矩阵初始值_1  (
    .out_1(\矩阵初始值_1_out_1 ), .out_2(\矩阵初始值_1_out_2 ), .out_3(\矩阵初始值_1_out_3 ), .out_4(\矩阵初始值_1_out_4 ));
  \矩阵乘法  \u_矩阵乘法_1  (
    .in_1(a11), .in_2(a12), .in_3(a21), .in_4(a22), .in_5(a11), .in_6(a12), .in_7(a21), .in_8(a22),
    .out_9(\矩阵乘法_1_out_9 ), .out_10(\矩阵乘法_1_out_10 ), .out_11(\矩阵乘法_1_out_11 ), .out_12(\矩阵乘法_1_out_12 ));
  Counter #(.width(1), .max('h1), .ongoal("stay")) counter_1 (
    .Q(counter_1_q), .clk(clock_1_out));  // open: load, D, count, carry, clr
  Clock clock_1 (.out(clock_1_out));
  \单位阵  \u_单位阵_1  (.out_1(\单位阵_1_out_1 ), .out_2(\单位阵_1_out_2 ), .out_3(\单位阵_1_out_3 ), .out_4(\单位阵_1_out_4 ));
  \矩阵mux  \u_矩阵mux_1  (
    .in_1(\单位阵_1_out_1 ), .in_2(\单位阵_1_out_2 ), .in_3(\单位阵_1_out_3 ), .in_4(\单位阵_1_out_4 ), .in_5(a11),
    .in_6(a12), .in_7(a21), .in_8(a22), .in_9(in_1), .out_10(\矩阵mux_1_out_10 ), .out_11(\矩阵mux_1_out_11 ),
    .out_12(\矩阵mux_1_out_12 ), .out_13(\矩阵mux_1_out_13 ));
  \矩阵mux  \u_矩阵mux_2  (
    .in_1(\矩阵初始值_1_out_1 ), .in_2(\矩阵初始值_1_out_2 ), .in_3(\矩阵初始值_1_out_3 ), .in_4(\矩阵初始值_1_out_4 ),
    .in_5(\矩阵乘法_1_out_9 ), .in_6(\矩阵乘法_1_out_10 ), .in_7(\矩阵乘法_1_out_11 ), .in_8(\矩阵乘法_1_out_12 ),
    .in_9(counter_1_q), .out_10(\矩阵mux_2_out_10 ), .out_11(\矩阵mux_2_out_11 ), .out_12(\矩阵mux_2_out_12 ),
    .out_13(\矩阵mux_2_out_13 ));
  not not_1 (not_1_out, in_2);
  Clock clock_2 (.out(clock_2_out));
  \寄存器矩阵  \u_寄存器矩阵_1  (
    .in_1(\矩阵mux_2_out_10 ), .in_2(\矩阵mux_2_out_11 ), .in_3(\矩阵mux_2_out_12 ), .in_4(\矩阵mux_2_out_13 ),
    .in_5(not_1_out), .out_6(a11), .out_7(a12), .out_8(a21), .out_9(a22));
  \单位阵  \u_单位阵_2  (.out_1(\单位阵_2_out_1 ), .out_2(\单位阵_2_out_2 ), .out_3(\单位阵_2_out_3 ), .out_4(\单位阵_2_out_4 ));
  \矩阵乘法  \u_矩阵乘法_2  (
    .in_1(s11), .in_2(s12), .in_3(s21), .in_4(s22), .in_5(\矩阵mux_1_out_10 ), .in_6(\矩阵mux_1_out_11 ),
    .in_7(\矩阵mux_1_out_12 ), .in_8(\矩阵mux_1_out_13 ), .out_9(\矩阵乘法_2_out_9 ), .out_10(\矩阵乘法_2_out_10 ),
    .out_11(\矩阵乘法_2_out_11 ), .out_12(\矩阵乘法_2_out_12 ));
  Counter #(.width(1), .max('h1), .ongoal("stay")) counter_2 (
    .Q(counter_2_q), .clk(clock_2_out));  // open: load, D, count, carry, clr
  // Probe on a11
  \矩阵mux  \u_矩阵mux_3  (
    .in_1(\单位阵_2_out_1 ), .in_2(\单位阵_2_out_2 ), .in_3(\单位阵_2_out_3 ), .in_4(\单位阵_2_out_4 ),
    .in_5(\矩阵乘法_2_out_9 ), .in_6(\矩阵乘法_2_out_10 ), .in_7(\矩阵乘法_2_out_11 ), .in_8(\矩阵乘法_2_out_12 ),
    .in_9(counter_2_q), .out_10(\矩阵mux_3_out_10 ), .out_11(\矩阵mux_3_out_11 ), .out_12(\矩阵mux_3_out_12 ),
    .out_13(\矩阵mux_3_out_13 ));
  // Probe on \矩阵mux_3_out_11 
  Multiplexer #(.width(32)) multiplexer_1 (.in0({32{1'b0}}), .in1(s12), .out(out_3), .sel(in_2));  // open: en
  // Probe on s12
  \寄存器矩阵  \u_寄存器矩阵_2  (
    .in_1(\矩阵mux_3_out_10 ), .in_2(\矩阵mux_3_out_11 ), .in_3(\矩阵mux_3_out_12 ), .in_4(\矩阵mux_3_out_13 ),
    .in_5(not_1_out), .out_6(s11), .out_7(s12), .out_8(s21), .out_9(s22));
  // Probe on a12
  // Probe on s22
  // Probe on a21
  // Probe on a22

  // Other names for the same wires on the sheet: free = in_2; low = in_1
endmodule

module \寄存器矩阵  (
  input  [31:0] in_1,
  input  [31:0] in_2,
  input  [31:0] in_3,
  input  [31:0] in_4,
  input  in_5,
  output [31:0] out_6,
  output [31:0] out_7,
  output [31:0] out_8,
  output [31:0] out_9
);

  wire clock_1_out;

  Register #(.width(32)) register_1 (.D(in_1), .en(in_5), .Q(out_6), .clk(clock_1_out));  // open: clr
  Register #(.width(32)) register_2 (.D(in_3), .en(in_5), .Q(out_8), .clk(clock_1_out));  // open: clr
  Clock clock_1 (.out(clock_1_out));
  Register #(.width(32)) register_3 (.D(in_2), .en(in_5), .Q(out_7), .clk(clock_1_out));  // open: clr
  Register #(.width(32)) register_4 (.D(in_4), .en(in_5), .Q(out_9), .clk(clock_1_out));  // open: clr
endmodule

module \单位阵  (
  output [31:0] out_1,
  output [31:0] out_2,
  output [31:0] out_3,
  output [31:0] out_4
);


  assign out_1 = 32'h1;
  assign out_2 = {32{1'b0}};
  assign out_3 = {32{1'b0}};
  assign out_4 = 32'h1;
endmodule

module \计数逻辑  (
  input  [31:0] in_1,
  output out_2,
  output out_3
);

  wire clock_1_out, comparator_1_eq, counter_1_q;
  wire [31:0] multiplexer_1_out, register_1_q, shifter_1_out;

  // Probe on shifter_1_out
  Shifter #(.width(32), .shift("lr")) shifter_1 (.in(register_1_q), .\dist (5'b00001), .out(shifter_1_out));
  Clock clock_1 (.out(clock_1_out));
  Multiplexer #(.width(32)) multiplexer_1 (
    .in0(in_1), .in1(shifter_1_out), .out(multiplexer_1_out), .sel(counter_1_q));  // open: en
  Counter #(.width(1), .max('h1), .ongoal("stay")) counter_1 (
    .Q(counter_1_q), .clk(clock_1_out));  // open: load, D, count, carry, clr
  Register #(.width(32)) register_1 (.D(multiplexer_1_out), .Q(register_1_q), .clk(clock_1_out));  // open: en, clr
  Multiplexer multiplexer_2 (.in0(1'b0), .in1(comparator_1_eq), .out(out_3), .sel(counter_1_q));  // open: en
  Comparator #(.width(32)) comparator_1 (.a(register_1_q), .b({32{1'b0}}), .eq(comparator_1_eq));  // open: gt, lt
  Bit_Extender #(.in_width(32), .out_width(1)) bit_extender_1 (.in(register_1_q), .out(out_2));
endmodule
