// Logisim project 斐波那契.circ as structural Verilog: 1 circuit, main circuit main
module main (
  input  [2:0] in_1,
  output [3:0] out_2
);

  wire clock_1_out, comparator_1_eq, nor_2_out, not_1_out;
  wire [0:0] nor_1_out;
  wire [3:0] adder_1_out, adder_2_out, adder_3_out, Fn_1_q, Fn_q, or_1_out, register_1_q;

  assign or_1_out = adder_1_out | {3'b000, nor_1_out[0]};  // OR_Gate or_1, 4 bits wide
  Adder #(.width(4)) adder_1 (.a(Fn_1_q), .b(Fn_q), .out(adder_1_out));  // open: cin, cout
  Adder #(.width(4)) adder_2 (.a({1'b0, in_1}), .b(4'b0010), .out(adder_2_out));  // open: cin, cout
  Adder #(.width(4)) adder_3 (.a(register_1_q), .b(4'b0001), .out(adder_3_out));  // open: cin, cout
  Clock clock_1 (.out(clock_1_out));
  Register #(.width(4)) Fn_1 (.D(or_1_out), .en(nor_2_out), .Q(Fn_1_q), .clk(clock_1_out));  // open: clr
  Register #(.width(4)) register_1 (.D(adder_3_out), .en(nor_2_out), .Q(register_1_q), .clk(clock_1_out));  // open: clr
  Register #(.width(4)) Fn (.D(Fn_1_q), .en(nor_2_out), .Q(Fn_q), .clk(clock_1_out));  // open: clr
  Comparator #(.width(4)) comparator_1 (.a(register_1_q), .b(adder_2_out), .eq(comparator_1_eq));  // open: gt, lt
  Register #(.width(4)) register_2 (.D(Fn_q), .en(nor_2_out), .Q(out_2), .clk(comparator_1_eq));  // open: clr
  not not_1 (not_1_out, register_1_q[0]);
  nor nor_1 (nor_1_out[0], not_1_out, register_1_q[1], register_1_q[2], register_1_q[3]);
  nor nor_2 (nor_2_out, out_2[0], out_2[1], out_2[2], out_2[3]);
endmodule
