// Logisim project 斐波那契——增强.circ as structural Verilog: 5 circuits, main circuit main
module main (
  input  [31:0] N,
  output [31:0] out_2
);

  wire beg, bitselector_1_out, clock, comparator_1_eq, power;
  wire [7:0] adder_1_out, n_t, subtractor_1_out;
  wire [31:0] a, am, b, bm, c, cm, d, dm, multiplexer_1_out, multiplexer_2_out, multiplexer_3_out,
       multiplexer_4_out, n2_2_mat_2_multi_1_out_9, n2_2_mat_2_multi_1_out_10, n2_2_mat_2_multi_1_out_11,
       n2_2_mat_2_multi_1_out_12, n4num_32bit_reg_1_out_8, n4num_32bit_reg_1_out_9, n4num_32bit_reg_1_out_10,
       n4num_32bit_reg_1_out_11, n4num_mux_1_out_10, n4num_mux_1_out_11, n4num_mux_1_out_12,
       n4num_mux_1_out_13, n4num_mux_2_out_10, n4num_mux_2_out_11, n4num_mux_2_out_12, n4num_mux_2_out_13;

  Adder adder_1 (.a(n_t), .b(8'h1), .out(adder_1_out));  // open: cin, cout
  Multiplexer #(.width(32)) multiplexer_1 (.in0(32'h1), .in1(a), .out(multiplexer_1_out), .sel(beg));  // open: en
  Multiplexer #(.width(32)) multiplexer_2 (.in0(32'h1), .in1(b), .out(multiplexer_2_out), .sel(beg));  // open: en
  Multiplexer #(.width(32)) multiplexer_3 (.in0(32'h1), .in1(c), .out(multiplexer_3_out), .sel(beg));  // open: en
  Multiplexer #(.width(32)) multiplexer_4 (.in0({32{1'b0}}), .in1(d), .out(multiplexer_4_out), .sel(beg));  // open: en
  _4num_32bit_Reg u_4num_32bit_reg_1 (
    .a(multiplexer_1_out), .b(multiplexer_2_out), .c(multiplexer_3_out), .d(multiplexer_4_out),
    .power(power), .clock(clock), .out_8(n4num_32bit_reg_1_out_8), .out_9(n4num_32bit_reg_1_out_9),
    .out_10(n4num_32bit_reg_1_out_10), .out_11(n4num_32bit_reg_1_out_11));  // open: clean
  Register register_1 (.D(adder_1_out), .en(power), .Q(n_t), .clk(clock));  // open: clr
  _2_2_Mat_self_multi u_2_2_mat_self_multi_1 (
    .a(n4num_32bit_reg_1_out_8), .b(n4num_32bit_reg_1_out_9), .c(n4num_32bit_reg_1_out_10),
    .d(n4num_32bit_reg_1_out_11), .out_5(a), .out_6(b), .out_7(c), .out_8(d));
  or or_1 (beg, n_t[0], n_t[1], n_t[2], n_t[3], n_t[4], n_t[5], n_t[6], n_t[7]);
  Subtractor subtractor_1 (.a(n_t), .b(8'h1), .out(subtractor_1_out));  // open: bin, bout
  Clock clock_1 (.out(clock));
  BitSelector #(.width(32)) bitselector_1 (.in(N), .out(bitselector_1_out), .sel(subtractor_1_out[4:0]));
  _4num_MUX u_4num_mux_1 (
    .a0(32'h1), .a1(n4num_32bit_reg_1_out_8), .b0({32{1'b0}}), .b1(n4num_32bit_reg_1_out_9), .c0({32{1'b0}}),
    .c1(n4num_32bit_reg_1_out_10), .d0(32'h1), .d1(n4num_32bit_reg_1_out_11), .sel(bitselector_1_out),
    .out_10(n4num_mux_1_out_10), .out_11(n4num_mux_1_out_11), .out_12(n4num_mux_1_out_12),
    .out_13(n4num_mux_1_out_13));
  _2_2_Mat_2_multi u_2_2_mat_2_multi_1 (
    .a2(am), .a1(n4num_mux_1_out_10), .b2(bm), .b1(n4num_mux_1_out_11), .c1(n4num_mux_1_out_12), .c2(cm),
    .d2(dm), .d1(n4num_mux_1_out_13), .out_9(n2_2_mat_2_multi_1_out_9), .out_10(n2_2_mat_2_multi_1_out_10),
    .out_11(n2_2_mat_2_multi_1_out_11), .out_12(n2_2_mat_2_multi_1_out_12));
  _4num_32bit_Reg u_4num_32bit_reg_2 (
    .a(n4num_mux_2_out_10), .b(n4num_mux_2_out_11), .c(n4num_mux_2_out_12), .d(n4num_mux_2_out_13),
    .power(power), .clock(clock), .out_8(am), .out_9(bm), .out_10(cm), .out_11(dm));  // open: clean
  _4num_MUX u_4num_mux_2 (
    .a0(32'h1), .a1(n2_2_mat_2_multi_1_out_9), .b0({32{1'b0}}), .b1(n2_2_mat_2_multi_1_out_10),
    .c0({32{1'b0}}), .c1(n2_2_mat_2_multi_1_out_11), .d0(32'h1), .d1(n2_2_mat_2_multi_1_out_12), .sel(beg),
    .out_10(n4num_mux_2_out_10), .out_11(n4num_mux_2_out_11), .out_12(n4num_mux_2_out_12),
    .out_13(n4num_mux_2_out_13));
  Register #(.width(32)) register_2 (.D(cm), .en(power), .Q(out_2), .clk(comparator_1_eq));  // open: clr
  Comparator #(.mode("unsigned")) comparator_1 (.a(n_t), .b(8'h21), .eq(comparator_1_eq));  // open: gt, lt
  Comparator #(.width(32), .mode("unsigned")) comparator_2 (.a(out_2), .b({32{1'b0}}), .eq(power));  // open: gt, lt
endmodule

module _4num_32bit_Reg (
  input  [31:0] a,
  input  [31:0] b,
  input  [31:0] c,
  input  clock,
  input  clean,
  input  [31:0] d,
  input  power,
  output [31:0] out_8,
  output [31:0] out_9,
  output [31:0] out_10,
  output [31:0] out_11
);

  Register #(.width(32)) register_1 (.D(a), .en(power), .Q(out_8), .clk(clock), .clr(clean));
  Register #(.width(32)) register_2 (.D(b), .en(power), .Q(out_9), .clk(clock), .clr(clean));
  Register #(.width(32)) register_3 (.D(c), .en(power), .Q(out_10), .clk(clock), .clr(clean));
  Register #(.width(32)) register_4 (.D(d), .en(power), .Q(out_11), .clk(clock), .clr(clean));
endmodule

module _2_2_Mat_self_multi (
  input  [31:0] a,
  input  [31:0] b,
  input  [31:0] c,
  input  [31:0] d,
  output [31:0] out_5,
  output [31:0] out_6,
  output [31:0] out_7,
  output [31:0] out_8
);

  wire [31:0] multiplier_1_out, multiplier_2_out, multiplier_3_out, multiplier_4_out, multiplier_5_out,
       multiplier_6_out, multiplier_7_out, multiplier_8_out;

  Multiplier #(.width(32)) multiplier_1 (.a(a), .b(a), .out(multiplier_1_out));  // open: cin, cout
  Multiplier #(.width(32)) multiplier_2 (.a(b), .b(c), .out(multiplier_2_out));  // open: cin, cout
  Multiplier #(.width(32)) multiplier_3 (.a(a), .b(b), .out(multiplier_3_out));  // open: cin, cout
  Multiplier #(.width(32)) multiplier_4 (.a(b), .b(d), .out(multiplier_4_out));  // open: cin, cout
  Multiplier #(.width(32)) multiplier_5 (.a(a), .b(c), .out(multiplier_5_out));  // open: cin, cout
  Multiplier #(.width(32)) multiplier_6 (.a(d), .b(c), .out(multiplier_6_out));  // open: cin, cout
  Multiplier #(.width(32)) multiplier_7 (.a(b), .b(c), .out(multiplier_7_out));  // open: cin, cout
  Multiplier #(.width(32)) multiplier_8 (.a(d), .b(d), .out(multiplier_8_out));  // open: cin, cout
  Adder #(.width(32)) adder_1 (.a(multiplier_1_out), .b(multiplier_2_out), .out(out_5));  // open: cin, cout
  Adder #(.width(32)) adder_2 (.a(multiplier_3_out), .b(multiplier_4_out), .out(out_6));  // open: cin, cout
  Adder #(.width(32)) adder_3 (.a(multiplier_5_out), .b(multiplier_6_out), .out(out_7));  // open: cin, cout
  Adder #(.width(32)) adder_4 (.a(multiplier_7_out), .b(multiplier_8_out), .out(out_8));  // open: cin, cout
endmodule

module _4num_MUX (
  input  sel,
  input  [31:0] a0,
  input  [31:0] a1,
  input  [31:0] b0,
  input  [31:0] b1,
  input  [31:0] c0,
  input  [31:0] c1,
  input  [31:0] d0,
  input  [31:0] d1,
  output [31:0] out_10,
  output [31:0] out_11,
  output [31:0] out_12,
  output [31:0] out_13
);

  Multiplexer #(.width(32)) multiplexer_1 (.in0(a0), .in1(a1), .out(out_10), .sel(sel));  // open: en
  Multiplexer #(.width(32)) multiplexer_2 (.in0(b0), .in1(b1), .out(out_11), .sel(sel));  // open: en
  Multiplexer #(.width(32)) multiplexer_3 (.in0(c0), .in1(c1), .out(out_12), .sel(sel));  // open: en
  Multiplexer #(.width(32)) multiplexer_4 (.in0(d0), .in1(d1), .out(out_13), .sel(sel));  // open: en
endmodule

module _2_2_Mat_2_multi (
  input  [31:0] a2,
  input  [31:0] a1,
  input  [31:0] b2,
  input  [31:0] b1,
  input  [31:0] c1,
  input  [31:0] c2,
  input  [31:0] d2,
  input  [31:0] d1,
  output [31:0] out_9,
  output [31:0] out_10,
  output [31:0] out_11,
  output [31:0] out_12
);

  wire [31:0] multiplier_1_out, multiplier_2_out, multiplier_3_out, multiplier_4_out, multiplier_5_out,
       multiplier_6_out, multiplier_7_out, multiplier_8_out;

  Multiplier #(.width(32)) multiplier_1 (.a(a1), .b(a2), .out(multiplier_1_out));  // open: cin, cout
  Multiplier #(.width(32)) multiplier_2 (.a(b1), .b(c2), .out(multiplier_2_out));  // open: cin, cout
  Multiplier #(.width(32)) multiplier_3 (.a(a1), .b(b2), .out(multiplier_3_out));  // open: cin, cout
  Multiplier #(.width(32)) multiplier_4 (.a(b1), .b(d2), .out(multiplier_4_out));  // open: cin, cout
  Multiplier #(.width(32)) multiplier_5 (.a(c1), .b(a2), .out(multiplier_5_out));  // open: cin, cout
  Multiplier #(.width(32)) multiplier_6 (.a(d1), .b(c2), .out(multiplier_6_out));  // open: cin, cout
  Multiplier #(.width(32)) multiplier_7 (.a(c1), .b(b2), .out(multiplier_7_out));  // open: cin, cout
  Multiplier #(.width(32)) multiplier_8 (.a(d1), .b(d2), .out(multiplier_8_out));  // open: cin, cout
  Adder #(.width(32)) adder_1 (.a(multiplier_1_out), .b(multiplier_2_out), .out(out_9));  // open: cin, cout
  Adder #(.width(32)) adder_2 (.a(multiplier_3_out), .b(multiplier_4_out), .out(out_10));  // open: cin, cout
  Adder #(.width(32)) adder_3 (.a(multiplier_5_out), .b(multiplier_6_out), .out(out_11));  // open: cin, cout
  Adder #(.width(32)) adder_4 (.a(multiplier_7_out), .b(multiplier_8_out), .out(out_12));  // open: cin, cout
endmodule
