// Logisim project 移位.circ as structural Verilog: 2 circuits, main circuit main
module main (
  input  [7:0] in_1,
  input  [2:0] in_2,
  output [7:0] out_3
);

  wire _000, _001, _010, _011, _100, _101, _110, _111, and_1_out, and_2_out, and_3_out, and_4_out, and_5_out,
       and_6_out, and_7_out, and_8_out, and_9_out, and_10_out, and_11_out, and_12_out, and_13_out,
       and_14_out, and_15_out, and_16_out, and_17_out, and_18_out, and_19_out, and_20_out, and_21_out,
       and_22_out, and_23_out, and_24_out, and_25_out, and_26_out, and_27_out, and_28_out, and_29_out,
       and_30_out, and_31_out, and_32_out, and_33_out, and_34_out, and_35_out, and_36_out, and_37_out,
       and_38_out, and_39_out, and_40_out, and_41_out, and_42_out, and_43_out, and_44_out, and_45_out,
       and_46_out, and_47_out, and_48_out, and_49_out, and_50_out, and_51_out, and_52_out, and_53_out,
       and_54_out, and_55_out, and_56_out, and_57_out, and_58_out, and_59_out, and_60_out, and_61_out,
       and_62_out, and_63_out, and_64_out;

  control control_1 (
    .in_1(in_2), ._000(_000), ._001(_001), ._010(_010), ._011(_011), ._100(_100), ._101(_101), ._110(_110),
    ._111(_111));
  and and_1 (and_1_out, 1'b0, _000);
  and and_2 (and_2_out, in_1[7], _001);
  and and_3 (and_3_out, in_1[6], _010);
  and and_4 (and_4_out, in_1[5], _011);
  and and_5 (and_5_out, in_1[4], _100);
  and and_6 (and_6_out, in_1[3], _101);
  and and_7 (and_7_out, in_1[2], _110);
  and and_8 (and_8_out, in_1[1], _111);
  or or_1 (out_3[0], and_1_out, and_2_out, and_3_out, and_4_out, and_5_out, and_6_out, and_7_out, and_8_out);
  and and_9 (and_9_out, in_1[0], _000);
  and and_10 (and_10_out, in_1[0], _001);
  and and_11 (and_11_out, in_1[7], _010);
  and and_12 (and_12_out, in_1[6], _011);
  and and_13 (and_13_out, in_1[5], _100);
  and and_14 (and_14_out, in_1[4], _101);
  and and_15 (and_15_out, in_1[3], _110);
  and and_16 (and_16_out, in_1[2], _111);
  or or_2 (out_3[1], and_9_out, and_10_out, and_11_out, and_12_out, and_13_out, and_14_out, and_15_out, and_16_out);
  and and_17 (and_17_out, in_1[1], _000);
  and and_18 (and_18_out, in_1[1], _001);
  and and_19 (and_19_out, in_1[0], _010);
  and and_20 (and_20_out, in_1[7], _011);
  and and_21 (and_21_out, in_1[6], _100);
  and and_22 (and_22_out, in_1[5], _101);
  and and_23 (and_23_out, in_1[4], _110);
  and and_24 (and_24_out, in_1[3], _111);
  or or_3 (out_3[2], and_17_out, and_18_out, and_19_out, and_20_out, and_21_out, and_22_out, and_23_out, and_24_out);
  and and_25 (and_25_out, in_1[2], _000);
  and and_26 (and_26_out, in_1[2], _001);
  and and_27 (and_27_out, in_1[1], _010);
  and and_28 (and_28_out, in_1[0], _011);
  and and_29 (and_29_out, in_1[7], _100);
  and and_30 (and_30_out, in_1[6], _101);
  and and_31 (and_31_out, in_1[5], _110);
  and and_32 (and_32_out, in_1[4], _111);
  or or_4 (out_3[3], and_25_out, and_26_out, and_27_out, and_28_out, and_29_out, and_30_out, and_31_out, and_32_out);
  and and_33 (and_33_out, in_1[3], _000);
  and and_34 (and_34_out, in_1[3], _001);
  and and_35 (and_35_out, in_1[2], _010);
  and and_36 (and_36_out, in_1[1], _011);
  and and_37 (and_37_out, in_1[0], _100);
  and and_38 (and_38_out, in_1[7], _101);
  and and_39 (and_39_out, in_1[6], _110);
  and and_40 (and_40_out, in_1[5], _111);
  or or_5 (out_3[4], and_33_out, and_34_out, and_35_out, and_36_out, and_37_out, and_38_out, and_39_out, and_40_out);
  and and_41 (and_41_out, in_1[4], _000);
  and and_42 (and_42_out, in_1[4], _001);
  and and_43 (and_43_out, in_1[3], _010);
  and and_44 (and_44_out, in_1[2], _011);
  and and_45 (and_45_out, in_1[1], _100);
  and and_46 (and_46_out, in_1[0], _101);
  and and_47 (and_47_out, in_1[7], _110);
  and and_48 (and_48_out, in_1[6], _111);
  or or_6 (out_3[5], and_41_out, and_42_out, and_43_out, and_44_out, and_45_out, and_46_out, and_47_out, and_48_out);
  and and_49 (and_49_out, in_1[5], _000);
  and and_50 (and_50_out, in_1[5], _001);
  and and_51 (and_51_out, in_1[4], _010);
  and and_52 (and_52_out, in_1[3], _011);
  and and_53 (and_53_out, in_1[2], _100);
  and and_54 (and_54_out, in_1[1], _101);
  and and_55 (and_55_out, in_1[0], _110);
  and and_56 (and_56_out, in_1[7], _111);
  or or_7 (out_3[6], and_49_out, and_50_out, and_51_out, and_52_out, and_53_out, and_54_out, and_55_out, and_56_out);
  and and_57 (and_57_out, in_1[6], _000);
  and and_58 (and_58_out, in_1[6], _001);
  and and_59 (and_59_out, in_1[5], _010);
  and and_60 (and_60_out, in_1[4], _011);
  and and_61 (and_61_out, in_1[3], _100);
  and and_62 (and_62_out, in_1[2], _101);
  and and_63 (and_63_out, in_1[1], _110);
  and and_64 (and_64_out, in_1[0], _111);
  or or_8 (out_3[7], and_57_out, and_58_out, and_59_out, and_60_out, and_61_out, and_62_out, and_63_out, and_64_out);

  // Other names for the same wires on the sheet: _0 = in_1[0]; _1 = in_1[1]; _2 = in_1[2]; _3 = in_1[3]; _4 = in_1[4];
  //   _5 = in_1[5]; _6 = in_1[6]; _7 = in_1[7]; q0 = out_3[0]; q1 = out_3[1]; q2 = out_3[2]; q3 = out_3[3];
  //   q4 = out_3[4]; q5 = out_3[5]; q6 = out_3[6]; q7 = out_3[7]
endmodule

module control (
  input  [2:0] in_1,
  output _000,
  output _001,
  output _010,
  output _011,
  output _100,
  output _101,
  output _110,
  output _111
);

  wire not_1_out, not_2_out, not_3_out;

  not not_1 (not_1_out, in_1[2]);
  not not_2 (not_2_out, in_1[1]);
  not not_3 (not_3_out, in_1[0]);
  and and_1 (_000, not_1_out, not_2_out, not_3_out);
  and and_2 (_001, not_1_out, not_2_out, in_1[0]);
  and and_3 (_010, not_1_out, in_1[1], not_3_out);
  and and_4 (_011, not_1_out, in_1[1], in_1[0]);
  and and_5 (_100, in_1[2], not_2_out, not_3_out);
  and and_6 (_101, in_1[2], not_2_out, in_1[0]);
  and and_7 (_110, in_1[2], in_1[1], not_3_out);
  and and_8 (_111, in_1[2], in_1[1], in_1[0]);
endmodule
